# Fritzing sketch pokrocili2-2-10-laser (saved by Fritzing 1.0.0d)
breadboards: 1

parts:
  S1 = SPST Switch [package=switch-spdt-smd]
  C1 = Electrolytic Capacitor [capacitance=0.47mF voltage=50V package="100 mil [THT, electrolytic]"]
  LASER = LED - 5mm [color="Red (633nm)" current=0.030A package="5 mm [THT]"]
  BAT1 = BATTERY-2 [package=battery-aaa]
  BAT2 = BATTERY-2 [package=battery-aaa]

nets:
  N1: S1.O, BAT1.+1
  N2: S1.P, C1.+
  N3: S1.S, LASER.anode
  N4: C1.-, LASER.cathode, BAT2.-1
  N5: BAT1.-1, BAT2.+1
