# Fritzing sketch pokrocili2-2-10-terc (saved by Fritzing 1.0.5)
breadboards: 1

parts:
  Mod1 = Microbit
  R1 = PHOTOCELL [part_number=0-20kOhm package=photocell]
  R2 = Resistor [tolerance=±5% power=0.25W resistance=10k package=THT]

nets:
  N1: Mod1.P1, R1.P$1, R2.Pin_1
  N2: Mod1.3V3, R2.Pin_0
  N3: Mod1.GND, R1.P$2

custom parts:
  Microbit: BBC Microbit Fritzing part. May 2019 expanded to include schematic and pcb views as well as breadboard. PCB view assumes an Adafruit PRODUCT ID: 3342 2x40 Right Angle through hole edge connector (although others will probably work as well). The pcb svg is custom (see forum article http://forum.fritzing.org/t/making-edge-connectors-and-both-side-smd-parts/7287 for an explaination if you need to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
